# Fritzing sketch garage-door-schema (saved by Fritzing 0.8.7b)
breadboards: 1

parts:
  Raspberry_Pi1 = Raspberry Pi (Model B)
  LED1 = LED - 5mm [color="Red (633nm)" package="5 mm [THT]"]
  LED2 = LED - 5mm [color="Red (633nm)" package="5 mm [THT]"]
  R1 = Resistor [tolerance=±5% resistance=220 package=THT]
  R2 = Resistor [tolerance=±5% resistance=220 package=THT]
  Relay_Module = Dual Channel Relay Module [part_number=SKU:20-018-100]
  Door_Open_Sensor = SWITCH-MOMENTARY-2 [package=tactile-switch-1101ne]
  Door_Closed_Sensor = SWITCH-MOMENTARY-2 [package=tactile-switch-1101ne]
  Door's_control_switch = mystery part, 3 pins [chip_label=?]

nets:
  N1: Raspberry_Pi1.pin_1:_3.3V, Door_Open_Sensor.2, Door_Closed_Sensor.1
  N2: Raspberry_Pi1.pin_2:_5V, Relay_Module.JD-VCC
  N3: Raspberry_Pi1.pin_6:_GND, R1.Pin_0, R2.Pin_0, Relay_Module.IN2, Relay_Module.GND
  N4: Raspberry_Pi1.pin_11:_GPIO_17, LED1.cathode, R1.Pin_1
  N5: Raspberry_Pi1.pin_12:_GPIO_18, LED2.cathode, R2.Pin_1
  N6: Raspberry_Pi1.pin_15:GPIO_22, Relay_Module.VCC
  N7: LED1.anode, Door_Open_Sensor.1
  N8: LED2.anode, Door_Closed_Sensor.2
  N9: Relay_Module.K2_Common, Door's_control_switch.pin2
  N10: Relay_Module.K2_Normally_Open, Door's_control_switch.pin3

notes:
  connect to the door control switch
  set the magnetic sensors to sense the door position
  VCC and GND are labeled incorrectly in the lower pingroup of the relay, they should be vise versa

custom parts:
  Raspberry Pi (Model B): Raspberry Pi Single-board Computer, Model B
  Dual Channel Relay Module: SainSmart 2-channel 5V Relay Module for Arduino and Raspberry Pi This is a 5V 2-Channel Relay interface board, Be able to control various appliances, and other equipments with large current. It can be controlled directly by Micro-controller (Arduino , 8051, AVR, PIC, DSP, ARM, ARM, MSP430, TTL logic)
